# Fritzing sketch Arduino単独システム例 (saved by Fritzing 0.9.2b)
perfboards: 4

parts:
  パーツ1 = Arduino Uno (Rev3)  # not connected
  Pro_Mini_3V3_8MHz1 = Arduino Pro Mini v13
  S2 = Akizuki slide switch IS-1250
  Power_plug6 = Power plug
  J97 = Arduino R3 6pin male header [package=THT]  # not connected
  Reset1 = Momentary Switch [package=ksa_sealed_tac_switch]
  IOH2 = female pin header, 10 pins [form="♀ (female)"]
  Power2 = female pin header, 8 pins [form="♀ (female)"]
  IOL2 = female pin header, 8 pins [form="♀ (female)"]
  AD2 = female pin header, 6 pins [form="♀ (female)"]
  VCC1 = Battery block 9V  # not connected
  S7 = Akizuki slide switch IS-2235
  S8 = Akizuki slide switch IS-2235
  ON/Sleep5 = male pin header, 5 pins [form="♂ (male)"]
  J131 = male pin header, 5 pins [form="♂ (male)"]
  RTC5 = RTC-8564NB [package="Module(DIP 8P)"]
  S9 = Akizuki slide switch IS-1250
  J132 = Arduino R3 6pin male header [package=THT]  # not connected
  Grove4 = Grove 3 Axis Digital Accelerometer 16g  # not connected
  microSD3 = MicroSD Breakout
  Card_detect2 = male pin header, 12 pins [form="♂ (male)"]
  J133 = male pin header, 12 pins [form="♂ (male)"]
  Chip_select2 = male pin header, 12 pins [form="♂ (male)"]
  J134 = male pin header, 12 pins [form="♂ (male)"]
  D12 = Schottky Diode [part_number=1N5817 package="300 mil [THT]"]
  D13 = Schottky Diode [part_number=1N5817 package="300 mil [THT]"]
  IOH11 = female pin header, 10 pins [form="♀ (female)"]
  INT6 = male pin header, 15 pins [form="♂ (male)"]
  J135 = male pin header, 15 pins [form="♂ (male)"]
  IOL11 = female pin header, 8 pins [form="♀ (female)"]
  Power10 = female pin header, 8 pins [form="♀ (female)"]
  AD11 = female pin header, 6 pins [form="♀ (female)"]
  BAT5 = Battery Holders [package=battcom_20mm_pth]
  J136 = Arduino R3 6pin male header [package=THT]  # not connected
  IOH12 = female pin header, 10 pins [form="♀ (female)"]
  IOL12 = female pin header, 8 pins [form="♀ (female)"]
  POWER2 = female pin header, 8 pins [form="♀ (female)"]
  AD12 = female pin header, 6 pins [form="♀ (female)"]  # not connected
  Grove5 = Grove Infrared Emitter  # not connected
  Grove6 = Grove 3 Axis Digital Accelerometer 16g  # not connected
  Xbee5 = SSCI-KIT-XBSOCKET
  J137 = Arduino R3 6pin male header [package=THT]  # not connected
  IOH13 = female pin header, 10 pins [form="♀ (female)"]
  J138 = male pin header, 11 pins [form="♂ (male)"]
  J139 = male pin header, 11 pins [form="♂ (male)"]
  J140 = male pin header, 11 pins [form="♂ (male)"]
  J141 = male pin header, 11 pins [form="♂ (male)"]
  J142 = male pin header, 11 pins [form="♂ (male)"]
  ON/Sleep6 = male pin header, 11 pins [form="♂ (male)"]
  Reset3 = male pin header, 11 pins [form="♂ (male)"]
  RSSI2 = male pin header, 11 pins [form="♂ (male)"]
  Associate2 = male pin header, 11 pins [form="♂ (male)"]
  Sleep_RQ2 = male pin header, 11 pins [form="♂ (male)"]
  Rx6 = male pin header, 15 pins [form="♂ (male)"]
  J143 = male pin header, 15 pins [form="♂ (male)"]
  Tx6 = male pin header, 15 pins [form="♂ (male)"]
  J144 = male pin header, 15 pins [form="♂ (male)"]
  INT7 = male pin header, 15 pins [form="♂ (male)"]
  J145 = male pin header, 15 pins [form="♂ (male)"]
  IOL13 = female pin header, 8 pins [form="♀ (female)"]
  Power11 = female pin header, 8 pins [form="♀ (female)"]
  AD13 = female pin header, 6 pins [form="♀ (female)"]

nets:
  N1: Pro_Mini_3V3_8MHz1.D0/TX, IOL2.pin8
  N2: Pro_Mini_3V3_8MHz1.D1/RX, IOL2.pin7
  N3: Pro_Mini_3V3_8MHz1.VCC, S2.pin1, S2.pin4
  GND: Pro_Mini_3V3_8MHz1.GND, Power_plug6.GND, Reset1.4, IOH2.pin4, Power2.pin6, Power2.pin7
  N4: Pro_Mini_3V3_8MHz1.A4, AD2.pin5
  N5: Pro_Mini_3V3_8MHz1.A5, AD2.pin6
  N6: Pro_Mini_3V3_8MHz1.RAW, Power_plug6.VCC, Power2.pin8
  N7: Pro_Mini_3V3_8MHz1.RESET, Reset1.2, Power2.pin3
  N8: Pro_Mini_3V3_8MHz1.A3, AD2.pin4
  N9: Pro_Mini_3V3_8MHz1.A2, AD2.pin3
  N10: Pro_Mini_3V3_8MHz1.A1, AD2.pin2
  N11: Pro_Mini_3V3_8MHz1.A0, AD2.pin1
  N12: Pro_Mini_3V3_8MHz1.D13/SCK, IOH2.pin5
  N13: Pro_Mini_3V3_8MHz1.D12/MISO, IOH2.pin6
  N14: Pro_Mini_3V3_8MHz1.D11_PWM/MOSI, IOH2.pin7
  N15: Pro_Mini_3V3_8MHz1.D10_PWM/SS, IOH2.pin8
  N16: Pro_Mini_3V3_8MHz1.D9_PWM, IOH2.pin9
  N17: Pro_Mini_3V3_8MHz1.D8, IOH2.pin10
  N18: Pro_Mini_3V3_8MHz1.D7, IOL2.pin1
  N19: Pro_Mini_3V3_8MHz1.D6_PWM, IOL2.pin2
  N20: Pro_Mini_3V3_8MHz1.D5_PWM, IOL2.pin3
  N21: Pro_Mini_3V3_8MHz1.D4, IOL2.pin4
  N22: Pro_Mini_3V3_8MHz1.D3_PWM, IOL2.pin5
  N23: Pro_Mini_3V3_8MHz1.D2, IOL2.pin6
  N24: S2.pin0, S2.pin3, Power2.pin4
  N25: S2.pin2, S2.pin5, Power2.pin5
  N26: S7.pin0, IOH11.pin10, J135.pin6
  N27: S7.pin1, RTC5.SDA
  N28: S7.pin2, AD11.pin5
  N29: S7.pin3, J135.pin8, IOL11.pin1
  N30: S7.pin4, RTC5.SCL
  N31: S7.pin5, AD11.pin6
  N32: S8.pin0, POWER2.pin5
  N33: S8.pin1, microSD3.5V
  N34: S8.pin4, microSD3.3v
  N35: S8.pin5, POWER2.pin4
  N36: ON/Sleep5.pin1, ON/Sleep5.pin2, ON/Sleep5.pin3, ON/Sleep5.pin4, ON/Sleep5.pin5, Xbee5.pin13, ON/Sleep6.pin1, ON/Sleep6.pin2, ON/Sleep6.pin3, ON/Sleep6.pin4, ON/Sleep6.pin5, ON/Sleep6.pin6, ON/Sleep6.pin7, ON/Sleep6.pin8, ON/Sleep6.pin9, ON/Sleep6.pin10, ON/Sleep6.pin11
  N37: J131.pin1, AD13.pin1
  N38: J131.pin2, AD13.pin2
  N39: J131.pin3, AD13.pin3
  N40: J131.pin4, AD13.pin4
  N41: J131.pin5, AD13.pin5
  N42: RTC5.INT, INT6.pin1, INT6.pin2, INT6.pin3, INT6.pin4, INT6.pin5, INT6.pin6, INT6.pin7, INT6.pin8, INT6.pin9, INT6.pin10, INT6.pin11, INT6.pin12, INT6.pin13, INT6.pin14, INT6.pin15
  N43: RTC5.GND, IOH11.pin4, Power10.pin6, Power10.pin7, BAT5.-
  N44: RTC5.VDD, D12.cathode, D13.cathode
  N45: S9.pin0, S9.pin3, Power10.pin5
  N46: S9.pin1, S9.pin4, D13.anode
  N47: S9.pin2, S9.pin5, Power10.pin4
  N48: microSD3.CD, Card_detect2.pin1, Card_detect2.pin2, Card_detect2.pin3, Card_detect2.pin4, Card_detect2.pin5, Card_detect2.pin6, Card_detect2.pin7, Card_detect2.pin8, Card_detect2.pin9, Card_detect2.pin10, Card_detect2.pin11, Card_detect2.pin12
  N49: microSD3.CS, Chip_select2.pin1, Chip_select2.pin2, Chip_select2.pin3, Chip_select2.pin4, Chip_select2.pin5, Chip_select2.pin6, Chip_select2.pin7, Chip_select2.pin8, Chip_select2.pin9, Chip_select2.pin10, Chip_select2.pin11, Chip_select2.pin12
  N50: microSD3.DI, IOH12.pin7
  N51: microSD3.DO, IOH12.pin6
  N52: microSD3.CLK, IOH12.pin5
  N53: microSD3.GND, IOH12.pin4, POWER2.pin6, POWER2.pin7
  N54: J133.pin1, J134.pin1, IOH12.pin8
  N55: J133.pin2, J134.pin2, IOH12.pin9
  N56: J133.pin3, J134.pin3, IOH12.pin10
  N57: J133.pin5, J134.pin5, IOL12.pin1
  N58: J133.pin6, J134.pin6, IOL12.pin2
  N59: J133.pin7, J134.pin7, IOL12.pin3
  N60: J133.pin8, J134.pin8, IOL12.pin4
  N61: J133.pin9, J134.pin9, IOL12.pin5
  N62: J133.pin10, J134.pin10, IOL12.pin6
  N63: J133.pin11, J134.pin11, IOL12.pin7
  N64: J133.pin12, J134.pin12, IOL12.pin8
  N65: D12.anode, BAT5.+
  N66: IOH11.pin5, J135.pin1
  N67: IOH11.pin6, J135.pin2
  N68: IOH11.pin7, J135.pin3
  N69: IOH11.pin8, J135.pin4
  N70: IOH11.pin9, J135.pin5
  N71: J135.pin9, IOL11.pin2
  N72: J135.pin10, IOL11.pin3
  N73: J135.pin11, IOL11.pin4
  N74: J135.pin12, IOL11.pin5
  N75: J135.pin13, IOL11.pin6
  N76: J135.pin14, IOL11.pin7
  N77: J135.pin15, IOL11.pin8
  N78: Xbee5.VCC, Power11.pin4
  N79: Xbee5.pin2, Tx6.pin1, Tx6.pin2, Tx6.pin3, Tx6.pin4, Tx6.pin5, Tx6.pin6, Tx6.pin7, Tx6.pin8, Tx6.pin9, Tx6.pin10, Tx6.pin11, Tx6.pin12, Tx6.pin13, Tx6.pin14, Tx6.pin15
  N80: Xbee5.pin3, Rx6.pin1, Rx6.pin2, Rx6.pin3, Rx6.pin4, Rx6.pin5, Rx6.pin6, Rx6.pin7, Rx6.pin8, Rx6.pin9, Rx6.pin10, Rx6.pin11, Rx6.pin12, Rx6.pin13, Rx6.pin14, Rx6.pin15
  N81: Xbee5.pin4, INT7.pin1, INT7.pin2, INT7.pin3, INT7.pin4, INT7.pin5, INT7.pin6, INT7.pin7, INT7.pin8, INT7.pin9, INT7.pin10, INT7.pin11, INT7.pin12, INT7.pin13, INT7.pin14, INT7.pin15
  N82: Xbee5.pin5, Reset3.pin1, Reset3.pin2, Reset3.pin3, Reset3.pin4, Reset3.pin5, Reset3.pin6, Reset3.pin7, Reset3.pin8, Reset3.pin9, Reset3.pin10, Reset3.pin11
  N83: Xbee5.pin6, RSSI2.pin1, RSSI2.pin2, RSSI2.pin3, RSSI2.pin4, RSSI2.pin5, RSSI2.pin6, RSSI2.pin7, RSSI2.pin8, RSSI2.pin9, RSSI2.pin10, RSSI2.pin11
  N84: Xbee5.pin9, Sleep_RQ2.pin1, Sleep_RQ2.pin2, Sleep_RQ2.pin3, Sleep_RQ2.pin4, Sleep_RQ2.pin5, Sleep_RQ2.pin6, Sleep_RQ2.pin7, Sleep_RQ2.pin8, Sleep_RQ2.pin9, Sleep_RQ2.pin10, Sleep_RQ2.pin11
  N85: Xbee5.GND, IOH13.pin4, Power11.pin6, Power11.pin7
  N86: Xbee5.pin15, Associate2.pin1, Associate2.pin2, Associate2.pin3, Associate2.pin4, Associate2.pin5, Associate2.pin6, Associate2.pin7, Associate2.pin8, Associate2.pin9, Associate2.pin10, Associate2.pin11
  N87: IOH13.pin5, J143.pin1, J144.pin1, J145.pin1
  N88: IOH13.pin6, J143.pin2, J144.pin2, J145.pin2
  N89: IOH13.pin7, J143.pin3, J144.pin3, J145.pin3
  N90: IOH13.pin8, J138.pin1, J139.pin1, J140.pin1, J141.pin1, J142.pin1, J143.pin4, J144.pin4, J145.pin4
  N91: IOH13.pin9, J138.pin2, J139.pin2, J140.pin2, J141.pin2, J142.pin2, J143.pin5, J144.pin5, J145.pin5
  N92: IOH13.pin10, J138.pin3, J139.pin3, J140.pin3, J141.pin3, J142.pin3, J143.pin6, J144.pin6, J145.pin6
  N93: J138.pin5, J139.pin5, J140.pin5, J141.pin5, J142.pin5, J143.pin8, J144.pin8, J145.pin8, IOL13.pin1
  N94: J138.pin6, J139.pin6, J140.pin6, J141.pin6, J142.pin6, J143.pin9, J144.pin9, J145.pin9, IOL13.pin2
  N95: J138.pin7, J139.pin7, J140.pin7, J141.pin7, J142.pin7, J143.pin10, J144.pin10, J145.pin10, IOL13.pin3
  N96: J138.pin8, J139.pin8, J140.pin8, J141.pin8, J142.pin8, J143.pin11, J144.pin11, J145.pin11, IOL13.pin4
  N97: J138.pin9, J139.pin9, J140.pin9, J141.pin9, J142.pin9, J143.pin12, J144.pin12, J145.pin12, IOL13.pin5
  N98: J138.pin10, J139.pin10, J140.pin10, J141.pin10, J142.pin10, J143.pin13, J144.pin13, J145.pin13, IOL13.pin6
  N99: J138.pin11, J139.pin11, J140.pin11, J141.pin11, J142.pin11, J143.pin14, J144.pin14, J145.pin14, IOL13.pin7
  N100: J143.pin15, J144.pin15, J145.pin15, IOL13.pin8

notes:
  もしくは

custom parts:
  Arduino Pro Mini v13: It's blue! It's thin! It's the Arduino Pro Mini! SparkFun's minimal design approach to Arduino. This is a 5V Arduino running the 16MHz bootloader. Arduino Pro Mini does not come with connectors populated so that you can solder in any connector or wire with any orientation you need. We recommend first time Arduino users start with the Uno R3. It's a great board that will get you up and running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
  Akizuki slide switch IS-1250: Akizuki slide switch is-1250 (P-01665)
  Power plug: 秋月電子通商 AE-DCJACK-DIPKIT-2.1mm-10A(通販コードK-06998)とその互換品(K06999,K-08415,K-08416)
  Arduino R3 6pin male header: Pin header for arduino R3
  Akizuki slide switch IS-2235: Akizuki slide switch is-2235 (P-02627)
  RTC-8564NB: Real Time Clock Module and I2C-BUS interface method. This product is a module of the SON 8-pin DIP package. Supply voltage 1.8-5.5V original version by KimuShige
  MicroSD Breakout: 5V-ready microSD Breakout with Level Shifter
  SSCI-KIT-XBSOCKET: Xbee pin conversion
