# Fritzing sketch Arduino連携システム例 (saved by Fritzing 0.9.2b)
perfboards: 5

parts:
  パーツ1 = Arduino Uno (Rev3)  # not connected
  Xbee2 = SSCI-KIT-XBSOCKET
  J93 = Arduino R3 6pin male header [package=THT]  # not connected
  IOH1 = female pin header, 10 pins [form="♀ (female)"]
  Rx1 = male pin header, 15 pins [form="♂ (male)"]
  J94 = male pin header, 15 pins [form="♂ (male)"]
  Tx1 = male pin header, 15 pins [form="♂ (male)"]
  J95 = male pin header, 15 pins [form="♂ (male)"]
  INT1 = male pin header, 15 pins [form="♂ (male)"]
  J96 = male pin header, 15 pins [form="♂ (male)"]
  IOL1 = female pin header, 8 pins [form="♀ (female)"]
  Power1 = female pin header, 8 pins [form="♀ (female)"]
  AD1 = female pin header, 6 pins [form="♀ (female)"]  # not connected
  Pro_Mini_3V3_8MHz1 = Arduino Pro Mini v13
  S2 = Akizuki slide switch IS-1250
  Power_plug6 = Power plug
  J97 = Arduino R3 6pin male header [package=THT]  # not connected
  Reset1 = Momentary Switch [package=ksa_sealed_tac_switch]
  IOH2 = female pin header, 10 pins [form="♀ (female)"]
  Power2 = female pin header, 8 pins [form="♀ (female)"]
  IOL2 = female pin header, 8 pins [form="♀ (female)"]
  AD2 = female pin header, 6 pins [form="♀ (female)"]
  U9 = RELAY-SIL05-1A72-71D [package=relay-g5v]
  J98 = Arduino R3 6pin male header [package=THT]  # not connected
  Signal_OUT1 = Grove Header 4pin 90 degree direct mount [package="90 degree"]
  Power_OUT1 = Grove Header 4pin 90 degree direct mount [package="90 degree"]
  IOH3 = female pin header, 10 pins [form="♀ (female)"]
  Rx2 = male pin header, 15 pins [form="♂ (male)"]
  Reset2 = male pin header, 15 pins [form="♂ (male)"]
  J99 = male pin header, 15 pins [form="♂ (male)"]
  Shutdown1 = male pin header, 15 pins [form="♂ (male)"]
  J100 = male pin header, 15 pins [form="♂ (male)"]
  J101 = male pin header, 15 pins [form="♂ (male)"]
  RelayControl1 = male pin header, 15 pins [form="♂ (male)"]
  J102 = male pin header, 15 pins [form="♂ (male)"]
  Tx2 = male pin header, 15 pins [form="♂ (male)"]
  J103 = male pin header, 15 pins [form="♂ (male)"]
  IOL3 = female pin header, 8 pins [form="♀ (female)"]
  Power3 = female pin header, 8 pins [form="♀ (female)"]
  AD3 = female pin header, 6 pins [form="♀ (female)"]  # not connected
  RTC3 = RTC-8564NB [package="Module(DIP 8P)"]
  S3 = Akizuki slide switch IS-1250
  J104 = Arduino R3 6pin male header [package=THT]  # not connected
  D7 = Schottky Diode [part_number=1N5817 package="300 mil [THT]"]
  D8 = Schottky Diode [part_number=1N5817 package="300 mil [THT]"]
  IOH4 = female pin header, 10 pins [form="♀ (female)"]
  INT2 = male pin header, 15 pins [form="♂ (male)"]
  J105 = male pin header, 15 pins [form="♂ (male)"]
  IOL4 = female pin header, 8 pins [form="♀ (female)"]
  Power4 = female pin header, 8 pins [form="♀ (female)"]
  AD4 = female pin header, 6 pins [form="♀ (female)"]
  BAT3 = Battery Holders [package=battcom_20mm_pth]
  J106 = Arduino R3 6pin male header [package=THT]  # not connected
  Power_IN1 = Grove Header 4pin 90 degree direct mount [package="90 degree"]
  Signal_IN1 = Grove Header 4pin 90 degree direct mount [package="90 degree"]
  LevelConverter1 = Bi-Directional Logic Level Converter [part_number=BOB-12009]
  IOH5 = female pin header, 10 pins [form="♀ (female)"]
  Shutdown2 = male pin header, 15 pins [form="♂ (male)"]
  J107 = male pin header, 15 pins [form="♂ (male)"]
  Rx3 = male pin header, 15 pins [form="♂ (male)"]
  J108 = male pin header, 15 pins [form="♂ (male)"]
  Tx3 = male pin header, 15 pins [form="♂ (male)"]
  J109 = male pin header, 15 pins [form="♂ (male)"]
  IOL5 = female pin header, 8 pins [form="♀ (female)"]
  Power5 = female pin header, 8 pins [form="♀ (female)"]
  AD5 = female pin header, 6 pins [form="♀ (female)"]  # not connected
  Grove1 = Grove 3 Axis Digital Accelerometer 16g  # not connected
  パーツ5 = Arduino MicroSD Shield  # not connected
  Grove2 = Grove Infrared Emitter  # not connected
  Grove3 = Grove 3 Axis Digital Accelerometer 16g  # not connected
  VCC1 = Battery block 9V  # not connected

nets:
  N1: Xbee2.VCC, Power1.pin4
  N2: Xbee2.pin2, Tx1.pin1, Tx1.pin2, Tx1.pin3, Tx1.pin4, Tx1.pin5, Tx1.pin6, Tx1.pin7, Tx1.pin8, Tx1.pin9, Tx1.pin10, Tx1.pin11, Tx1.pin12, Tx1.pin13, Tx1.pin14, Tx1.pin15
  N3: Xbee2.pin3, Rx1.pin1, Rx1.pin2, Rx1.pin3, Rx1.pin4, Rx1.pin5, Rx1.pin6, Rx1.pin7, Rx1.pin8, Rx1.pin9, Rx1.pin10, Rx1.pin11, Rx1.pin12, Rx1.pin13, Rx1.pin14, Rx1.pin15
  N4: Xbee2.pin4, INT1.pin1, INT1.pin2, INT1.pin3, INT1.pin4, INT1.pin5, INT1.pin6, INT1.pin7, INT1.pin8, INT1.pin9, INT1.pin10, INT1.pin11, INT1.pin12, INT1.pin13, INT1.pin14, INT1.pin15
  N5: Xbee2.pin7, Power1.pin3
  N6: Xbee2.GND, IOH1.pin4, Power1.pin6, Power1.pin7
  N7: IOH1.pin5, J94.pin1, J95.pin1, J96.pin1
  N8: IOH1.pin6, J94.pin2, J95.pin2, J96.pin2
  N9: IOH1.pin7, J94.pin3, J95.pin3, J96.pin3
  N10: IOH1.pin8, J94.pin4, J95.pin4, J96.pin4
  N11: IOH1.pin9, J94.pin5, J95.pin5, J96.pin5
  N12: IOH1.pin10, J94.pin6, J95.pin6, J96.pin6
  N13: J94.pin8, J95.pin8, J96.pin8, IOL1.pin1
  N14: J94.pin9, J95.pin9, J96.pin9, IOL1.pin2
  N15: J94.pin10, J95.pin10, J96.pin10, IOL1.pin3
  N16: J94.pin11, J95.pin11, J96.pin11, IOL1.pin4
  N17: J94.pin12, J95.pin12, J96.pin12, IOL1.pin5
  N18: J94.pin13, J95.pin13, J96.pin13, IOL1.pin6
  N19: J94.pin14, J95.pin14, J96.pin14, IOL1.pin7
  N20: J94.pin15, J95.pin15, J96.pin15, IOL1.pin8
  N21: Pro_Mini_3V3_8MHz1.D0/TX, IOL2.pin8
  N22: Pro_Mini_3V3_8MHz1.D1/RX, IOL2.pin7
  N23: Pro_Mini_3V3_8MHz1.VCC, S2.pin1, S2.pin4
  GND: Pro_Mini_3V3_8MHz1.GND, Power_plug6.GND, Reset1.4, IOH2.pin4, Power2.pin6, Power2.pin7
  N24: Pro_Mini_3V3_8MHz1.A4, AD2.pin5
  N25: Pro_Mini_3V3_8MHz1.A5, AD2.pin6
  N26: Pro_Mini_3V3_8MHz1.RAW, Power_plug6.VCC, Power2.pin8
  N27: Pro_Mini_3V3_8MHz1.RESET, Reset1.2, Power2.pin3
  N28: Pro_Mini_3V3_8MHz1.A3, AD2.pin4
  N29: Pro_Mini_3V3_8MHz1.A2, AD2.pin3
  N30: Pro_Mini_3V3_8MHz1.A1, AD2.pin2
  N31: Pro_Mini_3V3_8MHz1.A0, AD2.pin1
  N32: Pro_Mini_3V3_8MHz1.D13/SCK, IOH2.pin5
  N33: Pro_Mini_3V3_8MHz1.D12/MISO, IOH2.pin6
  N34: Pro_Mini_3V3_8MHz1.D11_PWM/MOSI, IOH2.pin7
  N35: Pro_Mini_3V3_8MHz1.D10_PWM/SS, IOH2.pin8
  N36: Pro_Mini_3V3_8MHz1.D9_PWM, IOH2.pin9
  N37: Pro_Mini_3V3_8MHz1.D8, IOH2.pin10
  N38: Pro_Mini_3V3_8MHz1.D7, IOL2.pin1
  N39: Pro_Mini_3V3_8MHz1.D6_PWM, IOL2.pin2
  N40: Pro_Mini_3V3_8MHz1.D5_PWM, IOL2.pin3
  N41: Pro_Mini_3V3_8MHz1.D4, IOL2.pin4
  N42: Pro_Mini_3V3_8MHz1.D3_PWM, IOL2.pin5
  N43: Pro_Mini_3V3_8MHz1.D2, IOL2.pin6
  N44: S2.pin0, S2.pin3, Power2.pin4
  N45: S2.pin2, S2.pin5, Power2.pin5
  N46: U9.IN, Power3.pin8
  N47: U9.CIN, RelayControl1.pin1, RelayControl1.pin2, RelayControl1.pin3, RelayControl1.pin4, RelayControl1.pin5, RelayControl1.pin6, RelayControl1.pin7, RelayControl1.pin8, RelayControl1.pin9, RelayControl1.pin10, RelayControl1.pin11, RelayControl1.pin12, RelayControl1.pin13, RelayControl1.pin14, RelayControl1.pin15
  N48: U9.COUT, Power_OUT1.4, IOH3.pin4, Power3.pin6, Power3.pin7
  N49: U9.OUT, Power_OUT1.3
  N50: Signal_OUT1.1, Reset2.pin1, Reset2.pin2, Reset2.pin3, Reset2.pin4, Reset2.pin5, Reset2.pin6, Reset2.pin7, Reset2.pin8, Reset2.pin9, Reset2.pin10, Reset2.pin11, Reset2.pin12, Reset2.pin13, Reset2.pin14, Reset2.pin15
  N51: Signal_OUT1.2, Shutdown1.pin1, Shutdown1.pin2, Shutdown1.pin3, Shutdown1.pin4, Shutdown1.pin5, Shutdown1.pin6, Shutdown1.pin7, Shutdown1.pin8, Shutdown1.pin9, Shutdown1.pin10, Shutdown1.pin11, Shutdown1.pin12, Shutdown1.pin13, Shutdown1.pin14, Shutdown1.pin15
  N52: Signal_OUT1.3, Rx2.pin1, Rx2.pin2, Rx2.pin3, Rx2.pin4, Rx2.pin5, Rx2.pin6, Rx2.pin7, Rx2.pin8, Rx2.pin9, Rx2.pin10, Rx2.pin11, Rx2.pin12, Rx2.pin13, Rx2.pin14, Rx2.pin15
  N53: Signal_OUT1.4, Tx2.pin1, Tx2.pin2, Tx2.pin3, Tx2.pin4, Tx2.pin5, Tx2.pin6, Tx2.pin7, Tx2.pin8, Tx2.pin9, Tx2.pin10, Tx2.pin11, Tx2.pin12, Tx2.pin13, Tx2.pin14, Tx2.pin15
  N54: Power_OUT1.2, Power3.pin4
  N55: IOH3.pin5, J99.pin1, J100.pin1, J101.pin1, J102.pin1, J103.pin1
  N56: IOH3.pin6, J99.pin2, J100.pin2, J101.pin2, J102.pin2, J103.pin2
  N57: IOH3.pin7, J99.pin3, J100.pin3, J101.pin3, J102.pin3, J103.pin3
  N58: IOH3.pin8, J99.pin4, J100.pin4, J101.pin4, J102.pin4, J103.pin4
  N59: IOH3.pin9, J99.pin5, J100.pin5, J101.pin5, J102.pin5, J103.pin5
  N60: IOH3.pin10, J99.pin6, J100.pin6, J101.pin6, J102.pin6, J103.pin6
  N61: J99.pin8, J100.pin8, J101.pin8, J102.pin8, J103.pin8, IOL3.pin1
  N62: J99.pin9, J100.pin9, J101.pin9, J102.pin9, J103.pin9, IOL3.pin2
  N63: J99.pin10, J100.pin10, J101.pin10, J102.pin10, J103.pin10, IOL3.pin3
  N64: J99.pin11, J100.pin11, J101.pin11, J102.pin11, J103.pin11, IOL3.pin4
  N65: J99.pin12, J100.pin12, J101.pin12, J102.pin12, J103.pin12, IOL3.pin5
  N66: J99.pin13, J100.pin13, J101.pin13, J102.pin13, J103.pin13, IOL3.pin6
  N67: J99.pin14, J100.pin14, J101.pin14, J102.pin14, J103.pin14, IOL3.pin7
  N68: J99.pin15, J100.pin15, J101.pin15, J102.pin15, J103.pin15, IOL3.pin8
  N69: RTC3.INT, INT2.pin1, INT2.pin2, INT2.pin3, INT2.pin4, INT2.pin5, INT2.pin6, INT2.pin7, INT2.pin8, INT2.pin9, INT2.pin10, INT2.pin11, INT2.pin12, INT2.pin13, INT2.pin14, INT2.pin15
  N70: RTC3.GND, IOH4.pin4, Power4.pin6, Power4.pin7, BAT3.-
  N71: RTC3.SDA, AD4.pin5
  N72: RTC3.SCL, AD4.pin6
  N73: RTC3.VDD, D7.cathode, D8.cathode
  N74: S3.pin0, S3.pin3, Power4.pin5
  N75: S3.pin1, S3.pin4, D8.anode
  N76: S3.pin2, S3.pin5, Power4.pin4
  N77: D7.anode, BAT3.+
  N78: IOH4.pin5, J105.pin1
  N79: IOH4.pin6, J105.pin2
  N80: IOH4.pin7, J105.pin3
  N81: IOH4.pin8, J105.pin4
  N82: IOH4.pin9, J105.pin5
  N83: IOH4.pin10, J105.pin6
  N84: J105.pin8, IOL4.pin1
  N85: J105.pin9, IOL4.pin2
  N86: J105.pin10, IOL4.pin3
  N87: J105.pin11, IOL4.pin4
  N88: J105.pin12, IOL4.pin5
  N89: J105.pin13, IOL4.pin6
  N90: J105.pin14, IOL4.pin7
  N91: J105.pin15, IOL4.pin8
  N92: Power_IN1.2, LevelConverter1.LV
  N93: Power_IN1.3, Power5.pin8
  N94: Power_IN1.4, LevelConverter1.GND, IOH5.pin4, Power5.pin6, Power5.pin7
  N95: Signal_IN1.1, LevelConverter1.LV4
  N96: Signal_IN1.2, LevelConverter1.LV3
  N97: Signal_IN1.3, LevelConverter1.LV2
  N98: Signal_IN1.4, LevelConverter1.LV1
  N99: LevelConverter1.HV4, Power5.pin3
  N100: LevelConverter1.HV3, Shutdown2.pin1, Shutdown2.pin2, Shutdown2.pin3, Shutdown2.pin4, Shutdown2.pin5, Shutdown2.pin6, Shutdown2.pin7, Shutdown2.pin8, Shutdown2.pin9, Shutdown2.pin10, Shutdown2.pin11, Shutdown2.pin12, Shutdown2.pin13, Shutdown2.pin14, Shutdown2.pin15
  N101: LevelConverter1.HV, Power5.pin5
  N102: LevelConverter1.HV2, Rx3.pin1, Rx3.pin2, Rx3.pin3, Rx3.pin4, Rx3.pin5, Rx3.pin6, Rx3.pin7, Rx3.pin8, Rx3.pin9, Rx3.pin10, Rx3.pin11, Rx3.pin12, Rx3.pin13, Rx3.pin14, Rx3.pin15
  N103: LevelConverter1.HV1, Tx3.pin1, Tx3.pin2, Tx3.pin3, Tx3.pin4, Tx3.pin5, Tx3.pin6, Tx3.pin7, Tx3.pin8, Tx3.pin9, Tx3.pin10, Tx3.pin11, Tx3.pin12, Tx3.pin13, Tx3.pin14, Tx3.pin15
  N104: IOH5.pin5, J107.pin1, J108.pin1, J109.pin1
  N105: IOH5.pin6, J107.pin2, J108.pin2, J109.pin2
  N106: IOH5.pin7, J107.pin3, J108.pin3, J109.pin3
  N107: IOH5.pin8, J107.pin4, J108.pin4, J109.pin4
  N108: IOH5.pin9, J107.pin5, J108.pin5, J109.pin5
  N109: IOH5.pin10, J107.pin6, J108.pin6, J109.pin6
  N110: J107.pin8, J108.pin8, J109.pin8, IOL5.pin1
  N111: J107.pin9, J108.pin9, J109.pin9, IOL5.pin2
  N112: J107.pin10, J108.pin10, J109.pin10, IOL5.pin3
  N113: J107.pin11, J108.pin11, J109.pin11, IOL5.pin4
  N114: J107.pin12, J108.pin12, J109.pin12, IOL5.pin5
  N115: J107.pin13, J108.pin13, J109.pin13, IOL5.pin6
  N116: J107.pin14, J108.pin14, J109.pin14, IOL5.pin7
  N117: J107.pin15, J108.pin15, J109.pin15, IOL5.pin8

custom parts:
  SSCI-KIT-XBSOCKET: Xbee pin conversion
  Arduino R3 6pin male header: Pin header for arduino R3
  Arduino Pro Mini v13: It's blue! It's thin! It's the Arduino Pro Mini! SparkFun's minimal design approach to Arduino. This is a 5V Arduino running the 16MHz bootloader. Arduino Pro Mini does not come with connectors populated so that you can solder in any connector or wire with any orientation you need. We recommend first time Arduino users start with the Uno R3. It's a great board that will get you up and running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
  Akizuki slide switch IS-1250: Akizuki slide switch is-1250 (P-01665)
  Power plug: 秋月電子通商 AE-DCJACK-DIPKIT-2.1mm-10A(通販コードK-06998)とその互換品(K06999,K-08415,K-08416)
  RELAY-SIL05-1A72-71D: MEDER SIL05-1A72-71D RSコンポーネンツ 349-2884
  Grove Header 4pin 90 degree direct mount: Header
  RTC-8564NB: Real Time Clock Module and I2C-BUS interface method. This product is a module of the SON 8-pin DIP package. Supply voltage 1.8-5.5V original version by KimuShige
  Bi-Directional Logic Level Converter: Description: If you've ever tried to connect a 3.3V device to a 5V system, you know what a challenge it can be. The SparkFun bi-directional logic level converter is a small device that safely steps down 5V signals to 3.3V AND steps up 3.3V to 5V at the same time. This level converter also works with 2.8V and 1.8V devices. What really separates this Logic level converter from our previous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
