# Fritzing sketch Kurumiロガー(シールド) (saved by Fritzing 0.9.2b)
perfboards: 1

parts:
  AD = female pin header, 6 pins [form="♀ (female)"]  # not connected
  Power = female pin header, 8 pins [form="♀ (female)"]
  IOL = female pin header, 8 pins [form="♀ (female)"]
  IOH = female pin header, 10 pins [form="♀ (female)"]
  DHT1 = DHT11 Humitidy and Temperature Sensor
  R1 = Resistor [tolerance=±5% resistance=10k package=THT]
  part = DeadOn RTC - DS3234 Breakout (for upside down) [part_number=BOB-10160]

nets:
  3.3V: Power.pin4, DHT1.VDD, R1.Pin_1, part.VCC
  GND: Power.pin6, Power.pin7, DHT1.GND, part.GND
  N1: IOL.pin4, DHT1.DATA, R1.Pin_0
  N2: IOH.pin5, part.SCLK
  MISO: IOH.pin6, part.MISO
  N3: IOH.pin7, part.MOSI
  Chip select: IOH.pin9, part.SS

custom parts:
  DHT11 Humitidy and Temperature Sensor: DHT11 Humidity and Temperature Sensor
  DeadOn RTC - DS3234 Breakout (for upside down): Description: Here is a real time clock based on the DS3234 Real Time Clock IC. The DS3234 is a low-cost, extremely accurate SPI bus real-time clock with an integrated temperature-compensated crystal oscillator and crystal. The RTC maintains seconds, minutes, hours, day, date, month, and year information. The date at the end of the month is automatically adjusted for months with fewer than 31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
