# Fritzing sketch Xbee,Arduino連携システム例 (saved by Fritzing 0.9.2b)
perfboards: 4

parts:
  パーツ1 = Arduino Uno (Rev3)  # not connected
  U9 = RELAY-SIL05-1A72-71D [package=relay-g5v]
  J98 = Arduino R3 6pin male header [package=THT]  # not connected
  Signal_OUT1 = Grove Header 4pin 90 degree direct mount [package="90 degree"]
  Power_OUT1 = Grove Header 4pin 90 degree direct mount [package="90 degree"]
  IOH3 = female pin header, 10 pins [form="♀ (female)"]
  Rx2 = male pin header, 15 pins [form="♂ (male)"]
  Reset2 = male pin header, 15 pins [form="♂ (male)"]
  J99 = male pin header, 15 pins [form="♂ (male)"]
  Shutdown1 = male pin header, 15 pins [form="♂ (male)"]
  J100 = male pin header, 15 pins [form="♂ (male)"]
  J101 = male pin header, 15 pins [form="♂ (male)"]
  RelayControl1 = male pin header, 15 pins [form="♂ (male)"]
  J102 = male pin header, 15 pins [form="♂ (male)"]
  Tx2 = male pin header, 15 pins [form="♂ (male)"]
  J103 = male pin header, 15 pins [form="♂ (male)"]
  IOL3 = female pin header, 8 pins [form="♀ (female)"]
  Power3 = female pin header, 8 pins [form="♀ (female)"]
  AD3 = female pin header, 6 pins [form="♀ (female)"]  # not connected
  RTC3 = RTC-8564NB [package="Module(DIP 8P)"]
  S3 = Akizuki slide switch IS-1250
  J104 = Arduino R3 6pin male header [package=THT]  # not connected
  D7 = Schottky Diode [part_number=1N5817 package="300 mil [THT]"]
  D8 = Schottky Diode [part_number=1N5817 package="300 mil [THT]"]
  IOH4 = female pin header, 10 pins [form="♀ (female)"]
  INT2 = male pin header, 15 pins [form="♂ (male)"]
  J105 = male pin header, 15 pins [form="♂ (male)"]
  IOL4 = female pin header, 8 pins [form="♀ (female)"]
  Power4 = female pin header, 8 pins [form="♀ (female)"]
  AD4 = female pin header, 6 pins [form="♀ (female)"]
  BAT3 = Battery Holders [package=battcom_20mm_pth]
  J106 = Arduino R3 6pin male header [package=THT]  # not connected
  Power_IN1 = Grove Header 4pin 90 degree direct mount [package="90 degree"]
  Signal_IN1 = Grove Header 4pin 90 degree direct mount [package="90 degree"]
  LevelConverter1 = Bi-Directional Logic Level Converter [part_number=BOB-12009]
  IOH5 = female pin header, 10 pins [form="♀ (female)"]
  Shutdown2 = male pin header, 15 pins [form="♂ (male)"]
  J107 = male pin header, 15 pins [form="♂ (male)"]
  Rx3 = male pin header, 15 pins [form="♂ (male)"]
  J108 = male pin header, 15 pins [form="♂ (male)"]
  Tx3 = male pin header, 15 pins [form="♂ (male)"]
  J109 = male pin header, 15 pins [form="♂ (male)"]
  IOL5 = female pin header, 8 pins [form="♀ (female)"]
  Power5 = female pin header, 8 pins [form="♀ (female)"]
  AD5 = female pin header, 6 pins [form="♀ (female)"]  # not connected
  Grove1 = Grove 3 Axis Digital Accelerometer 16g  # not connected
  パーツ5 = Arduino MicroSD Shield  # not connected
  Grove2 = Grove Infrared Emitter  # not connected
  Grove3 = Grove 3 Axis Digital Accelerometer 16g  # not connected
  VCC1 = Battery block 9V  # not connected
  Power_plug7 = Power plug
  Xbee3 = SSCI-KIT-XBSOCKET
  J110 = Arduino R3 6pin male header [package=THT]  # not connected
  Vol1 = Trimmer Potentiometer [maximum_resistance=0.1MΩ package=THT]
  Reset3 = Momentary Switch [package=ksa_sealed_tac_switch]
  IOH6 = female pin header, 10 pins [form="♀ (female)"]
  IOL6 = female pin header, 8 pins [form="♀ (female)"]
  Power6 = female pin header, 8 pins [form="♀ (female)"]
  J111 = male pin header, 3 pins [form="♂ (male)"]
  AD6 = female pin header, 6 pins [form="♀ (female)"]
  R2 = Resistor [tolerance=±5% resistance=10k package=THT]
  AE-MOD2 = AE-XCL101C331BR-G

nets:
  N1: U9.IN, Power3.pin8
  N2: U9.CIN, RelayControl1.pin1, RelayControl1.pin2, RelayControl1.pin3, RelayControl1.pin4, RelayControl1.pin5, RelayControl1.pin6, RelayControl1.pin7, RelayControl1.pin8, RelayControl1.pin9, RelayControl1.pin10, RelayControl1.pin11, RelayControl1.pin12, RelayControl1.pin13, RelayControl1.pin14, RelayControl1.pin15
  N3: U9.COUT, Power_OUT1.4, IOH3.pin4, Power3.pin6, Power3.pin7
  N4: U9.OUT, Power_OUT1.3
  N5: Signal_OUT1.1, Reset2.pin1, Reset2.pin2, Reset2.pin3, Reset2.pin4, Reset2.pin5, Reset2.pin6, Reset2.pin7, Reset2.pin8, Reset2.pin9, Reset2.pin10, Reset2.pin11, Reset2.pin12, Reset2.pin13, Reset2.pin14, Reset2.pin15
  N6: Signal_OUT1.2, Shutdown1.pin1, Shutdown1.pin2, Shutdown1.pin3, Shutdown1.pin4, Shutdown1.pin5, Shutdown1.pin6, Shutdown1.pin7, Shutdown1.pin8, Shutdown1.pin9, Shutdown1.pin10, Shutdown1.pin11, Shutdown1.pin12, Shutdown1.pin13, Shutdown1.pin14, Shutdown1.pin15
  N7: Signal_OUT1.3, Rx2.pin1, Rx2.pin2, Rx2.pin3, Rx2.pin4, Rx2.pin5, Rx2.pin6, Rx2.pin7, Rx2.pin8, Rx2.pin9, Rx2.pin10, Rx2.pin11, Rx2.pin12, Rx2.pin13, Rx2.pin14, Rx2.pin15
  N8: Signal_OUT1.4, Tx2.pin1, Tx2.pin2, Tx2.pin3, Tx2.pin4, Tx2.pin5, Tx2.pin6, Tx2.pin7, Tx2.pin8, Tx2.pin9, Tx2.pin10, Tx2.pin11, Tx2.pin12, Tx2.pin13, Tx2.pin14, Tx2.pin15
  N9: Power_OUT1.2, Power3.pin4
  N10: IOH3.pin5, J99.pin1, J100.pin1, J101.pin1, J102.pin1, J103.pin1
  N11: IOH3.pin6, J99.pin2, J100.pin2, J101.pin2, J102.pin2, J103.pin2
  N12: IOH3.pin7, J99.pin3, J100.pin3, J101.pin3, J102.pin3, J103.pin3
  N13: IOH3.pin8, J99.pin4, J100.pin4, J101.pin4, J102.pin4, J103.pin4
  N14: IOH3.pin9, J99.pin5, J100.pin5, J101.pin5, J102.pin5, J103.pin5
  N15: IOH3.pin10, J99.pin6, J100.pin6, J101.pin6, J102.pin6, J103.pin6
  N16: J99.pin8, J100.pin8, J101.pin8, J102.pin8, J103.pin8, IOL3.pin1
  N17: J99.pin9, J100.pin9, J101.pin9, J102.pin9, J103.pin9, IOL3.pin2
  N18: J99.pin10, J100.pin10, J101.pin10, J102.pin10, J103.pin10, IOL3.pin3
  N19: J99.pin11, J100.pin11, J101.pin11, J102.pin11, J103.pin11, IOL3.pin4
  N20: J99.pin12, J100.pin12, J101.pin12, J102.pin12, J103.pin12, IOL3.pin5
  N21: J99.pin13, J100.pin13, J101.pin13, J102.pin13, J103.pin13, IOL3.pin6
  N22: J99.pin14, J100.pin14, J101.pin14, J102.pin14, J103.pin14, IOL3.pin7
  N23: J99.pin15, J100.pin15, J101.pin15, J102.pin15, J103.pin15, IOL3.pin8
  N24: RTC3.INT, INT2.pin1, INT2.pin2, INT2.pin3, INT2.pin4, INT2.pin5, INT2.pin6, INT2.pin7, INT2.pin8, INT2.pin9, INT2.pin10, INT2.pin11, INT2.pin12, INT2.pin13, INT2.pin14, INT2.pin15
  N25: RTC3.GND, IOH4.pin4, Power4.pin6, Power4.pin7, BAT3.-
  N26: RTC3.SDA, AD4.pin5
  N27: RTC3.SCL, AD4.pin6
  N28: RTC3.VDD, D7.cathode, D8.cathode
  N29: S3.pin0, S3.pin3, Power4.pin5
  N30: S3.pin1, S3.pin4, D8.anode
  N31: S3.pin2, S3.pin5, Power4.pin4
  N32: D7.anode, BAT3.+
  N33: IOH4.pin5, J105.pin1
  N34: IOH4.pin6, J105.pin2
  N35: IOH4.pin7, J105.pin3
  N36: IOH4.pin8, J105.pin4
  N37: IOH4.pin9, J105.pin5
  N38: IOH4.pin10, J105.pin6
  N39: J105.pin8, IOL4.pin1
  N40: J105.pin9, IOL4.pin2
  N41: J105.pin10, IOL4.pin3
  N42: J105.pin11, IOL4.pin4
  N43: J105.pin12, IOL4.pin5
  N44: J105.pin13, IOL4.pin6
  N45: J105.pin14, IOL4.pin7
  N46: J105.pin15, IOL4.pin8
  N47: Power_IN1.2, LevelConverter1.LV
  N48: Power_IN1.3, Power5.pin8
  N49: Power_IN1.4, LevelConverter1.GND, IOH5.pin4, Power5.pin6, Power5.pin7
  N50: Signal_IN1.1, LevelConverter1.LV4
  N51: Signal_IN1.2, LevelConverter1.LV3
  N52: Signal_IN1.3, LevelConverter1.LV2
  N53: Signal_IN1.4, LevelConverter1.LV1
  N54: LevelConverter1.HV4, Power5.pin3
  N55: LevelConverter1.HV3, Shutdown2.pin1, Shutdown2.pin2, Shutdown2.pin3, Shutdown2.pin4, Shutdown2.pin5, Shutdown2.pin6, Shutdown2.pin7, Shutdown2.pin8, Shutdown2.pin9, Shutdown2.pin10, Shutdown2.pin11, Shutdown2.pin12, Shutdown2.pin13, Shutdown2.pin14, Shutdown2.pin15
  N56: LevelConverter1.HV, Power5.pin5
  N57: LevelConverter1.HV2, Rx3.pin1, Rx3.pin2, Rx3.pin3, Rx3.pin4, Rx3.pin5, Rx3.pin6, Rx3.pin7, Rx3.pin8, Rx3.pin9, Rx3.pin10, Rx3.pin11, Rx3.pin12, Rx3.pin13, Rx3.pin14, Rx3.pin15
  N58: LevelConverter1.HV1, Tx3.pin1, Tx3.pin2, Tx3.pin3, Tx3.pin4, Tx3.pin5, Tx3.pin6, Tx3.pin7, Tx3.pin8, Tx3.pin9, Tx3.pin10, Tx3.pin11, Tx3.pin12, Tx3.pin13, Tx3.pin14, Tx3.pin15
  N59: IOH5.pin5, J107.pin1, J108.pin1, J109.pin1
  N60: IOH5.pin6, J107.pin2, J108.pin2, J109.pin2
  N61: IOH5.pin7, J107.pin3, J108.pin3, J109.pin3
  N62: IOH5.pin8, J107.pin4, J108.pin4, J109.pin4
  N63: IOH5.pin9, J107.pin5, J108.pin5, J109.pin5
  N64: IOH5.pin10, J107.pin6, J108.pin6, J109.pin6
  N65: J107.pin8, J108.pin8, J109.pin8, IOL5.pin1
  N66: J107.pin9, J108.pin9, J109.pin9, IOL5.pin2
  N67: J107.pin10, J108.pin10, J109.pin10, IOL5.pin3
  N68: J107.pin11, J108.pin11, J109.pin11, IOL5.pin4
  N69: J107.pin12, J108.pin12, J109.pin12, IOL5.pin5
  N70: J107.pin13, J108.pin13, J109.pin13, IOL5.pin6
  N71: J107.pin14, J108.pin14, J109.pin14, IOL5.pin7
  N72: J107.pin15, J108.pin15, J109.pin15, IOL5.pin8
  GND: Power_plug7.GND, Xbee3.GND, Vol1.leg2, Reset3.3, IOH6.pin4, Power6.pin6, Power6.pin7, J111.pin3, AE-MOD2.VSS
  N73: Power_plug7.VCC, Power6.pin8, AE-MOD2.Vbat, AE-MOD2.CE
  N74: Xbee3.VCC, Vol1.leg1, Power6.pin4, R2.Pin_1, AE-MOD2.Vout
  N75: Xbee3.pin2, IOL6.pin7
  N76: Xbee3.pin3, IOL6.pin8
  N77: Xbee3.pin4, IOH6.pin6
  N78: Xbee3.pin5, Reset3.2, Power6.pin3
  N79: Xbee3.pin6, IOH6.pin8
  N80: Xbee3.pin7, IOH6.pin7
  N81: Xbee3.pin9, IOH6.pin10
  N82: Xbee3.pin11, IOL6.pin4
  N83: Xbee3.pin12, IOL6.pin1
  N84: Xbee3.pin13, IOL6.pin5
  N85: Xbee3.pin14, J111.pin2
  N86: Xbee3.pin15, IOL6.pin3
  N87: Xbee3.pin16, IOL6.pin2
  N88: Xbee3.pin17, AD6.pin4
  N89: Xbee3.pin18, AD6.pin3
  N90: Xbee3.pin19, AD6.pin2
  N91: Xbee3.pin20, AD6.pin1
  N92: Vol1.wiper, J111.pin1
  N93: Reset3.1, R2.Pin_0

custom parts:
  RELAY-SIL05-1A72-71D: MEDER SIL05-1A72-71D RSコンポーネンツ 349-2884
  Arduino R3 6pin male header: Pin header for arduino R3
  Grove Header 4pin 90 degree direct mount: Header
  RTC-8564NB: Real Time Clock Module and I2C-BUS interface method. This product is a module of the SON 8-pin DIP package. Supply voltage 1.8-5.5V original version by KimuShige
  Akizuki slide switch IS-1250: Akizuki slide switch is-1250 (P-01665)
  Bi-Directional Logic Level Converter: Description: If you've ever tried to connect a 3.3V device to a 5V system, you know what a challenge it can be. The SparkFun bi-directional logic level converter is a small device that safely steps down 5V signals to 3.3V AND steps up 3.3V to 5V at the same time. This level converter also works with 2.8V and 1.8V devices. What really separates this Logic level converter from our previous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
  Power plug: 秋月電子通商 AE-DCJACK-DIPKIT-2.1mm-10A(通販コードK-06998)とその互換品(K06999,K-08415,K-08416)
  SSCI-KIT-XBSOCKET: Xbee pin conversion
