# Fritzing sketch DeadOnRTCシールド (saved by Fritzing 0.9.2b)
perfboards: 1

parts:
  IOH = female pin header, 10 pins [form="♀ (female)"]
  IOL = female pin header, 8 pins [form="♀ (female)"]
  AD = female pin header, 6 pins [form="♀ (female)"]  # not connected
  Power = female pin header, 8 pins [form="♀ (female)"]
  S1 = Akizuki slide switch IS-1250
  J3 = Arduino R3 6pin male header [package=THT]  # not connected
  BOB-1 = DeadOn RTC - DS3234 Breakout (for upside down) [part_number=BOB-10160]
  chip_select = male pin header, 12 pins [form="♂ (male)"]
  J1 = male pin header, 12 pins [form="♂ (male)"]
  SQW = male pin header, 12 pins [form="♂ (male)"]
  J2 = male pin header, 12 pins [form="♂ (male)"]

nets:
  GND: IOH.pin4, Power.pin6, Power.pin7, BOB-1.GND
  N1: IOH.pin5, BOB-1.SCLK
  MISO: IOH.pin6, BOB-1.MISO
  N2: IOH.pin7, BOB-1.MOSI
  N3: IOH.pin8, J1.pin1, J2.pin1
  N4: IOH.pin9, J1.pin2, J2.pin2
  N5: IOH.pin10, J1.pin3, J2.pin3
  N6: IOL.pin1, J1.pin5, J2.pin5
  N7: IOL.pin2, J1.pin6, J2.pin6
  N8: IOL.pin3, J1.pin7, J2.pin7
  N9: IOL.pin4, J1.pin8, J2.pin8
  N10: IOL.pin5, J1.pin9, J2.pin9
  N11: IOL.pin6, J1.pin10, J2.pin10
  N12: IOL.pin7, J1.pin11, J2.pin11
  N13: IOL.pin8, J1.pin12, J2.pin12
  N14: Power.pin4, S1.pin2, S1.pin5
  N15: Power.pin5, S1.pin0, S1.pin3
  N16: S1.pin1, S1.pin4, BOB-1.VCC
  chip select: BOB-1.SS, chip_select.pin1, chip_select.pin2, chip_select.pin3, chip_select.pin4, chip_select.pin5, chip_select.pin6, chip_select.pin7, chip_select.pin8, chip_select.pin9, chip_select.pin10, chip_select.pin11, chip_select.pin12
  N17: BOB-1.INT/SQW, SQW.pin1, SQW.pin2, SQW.pin3, SQW.pin4, SQW.pin5, SQW.pin6, SQW.pin7, SQW.pin8, SQW.pin9, SQW.pin10, SQW.pin11, SQW.pin12

custom parts:
  Akizuki slide switch IS-1250: Akizuki slide switch is-1250 (P-01665)
  Arduino R3 6pin male header: Pin header for arduino R3
  DeadOn RTC - DS3234 Breakout (for upside down): Description: Here is a real time clock based on the DS3234 Real Time Clock IC. The DS3234 is a low-cost, extremely accurate SPI bus real-time clock with an integrated temperature-compensated crystal oscillator and crystal. The RTC maintains seconds, minutes, hours, day, date, month, and year information. The date at the end of the month is automatically adjusted for months with fewer than 31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
