# Fritzing sketch RTC8564NBシールド (saved by Fritzing 0.9.2b)
perfboards: 1

parts:
  IOH = female pin header, 10 pins [form="♀ (female)"]
  IOL = female pin header, 8 pins [form="♀ (female)"]
  AD = female pin header, 6 pins [form="♀ (female)"]
  BAT = Battery Holders [package=battcom_20mm_pth]
  J1 = male pin header, 15 pins [form="♂ (male)"]
  D1 = Schottky Diode [part_number=1N5817 package="300 mil [THT]"]
  D2 = Schottky Diode [part_number=1N5817 package="300 mil [THT]"]
  INT = male pin header, 15 pins [form="♂ (male)"]
  Power = female pin header, 8 pins [form="♀ (female)"]
  S1 = Akizuki slide switch IS-1250
  J2 = Arduino R3 6pin male header [package=THT]  # not connected
  RTC1 = RTC-8564NB [package="Module(DIP 8P)"]
  J5 = male pin header, 3 pins [form="♂ (male)"]
  J6 = male pin header, 3 pins [form="♂ (male)"]
  J7 = male pin header, 3 pins [form="♂ (male)"]
  J8 = male pin header, 3 pins [form="♂ (male)"]

nets:
  SCL3: IOH.pin1, J8.pin1
  SDA3: IOH.pin2, J6.pin1
  GND: IOH.pin4, BAT.-, Power.pin6, Power.pin7, RTC1.GND
  N1: IOH.pin5, J1.pin1
  N2: IOH.pin6, J1.pin2
  N3: IOH.pin7, J1.pin3
  N4: IOH.pin8, J1.pin4
  N5: IOH.pin9, J1.pin5
  SDA2: IOH.pin10, J1.pin6, J6.pin2
  SCL2: IOL.pin1, J1.pin8, J8.pin2
  N6: IOL.pin2, J1.pin9
  N7: IOL.pin3, J1.pin10
  N8: IOL.pin4, J1.pin11
  N9: IOL.pin5, J1.pin12
  N10: IOL.pin6, J1.pin13
  N11: IOL.pin7, J1.pin14
  N12: IOL.pin8, J1.pin15
  N13: AD.pin5, J6.pin3
  N14: AD.pin6, J8.pin3
  N15: BAT.+, D2.anode
  N16: D1.cathode, D2.cathode, RTC1.VDD
  N17: D1.anode, S1.pin1, S1.pin4
  N18: INT.pin1, INT.pin2, INT.pin3, INT.pin4, INT.pin5, INT.pin6, INT.pin7, INT.pin8, INT.pin9, INT.pin10, INT.pin11, INT.pin12, INT.pin13, INT.pin14, INT.pin15, RTC1.INT
  N19: Power.pin4, S1.pin2, S1.pin5
  N20: Power.pin5, S1.pin0, S1.pin3
  SDA: RTC1.SDA, J5.pin1, J5.pin2, J5.pin3
  SCL: RTC1.SCL, J7.pin1, J7.pin2, J7.pin3

custom parts:
  Akizuki slide switch IS-1250: Akizuki slide switch is-1250 (P-01665)
  Arduino R3 6pin male header: Pin header for arduino R3
  RTC-8564NB: Real Time Clock Module and I2C-BUS interface method. This product is a module of the SON 8-pin DIP package. Supply voltage 1.8-5.5V original version by KimuShige
