# Fritzing sketch grove3v3シールド (saved by Fritzing 0.9.2b)
perfboards: 1

parts:
  IOL = female pin header, 8 pins [form="♀ (female)"]
  IOH = female pin header, 10 pins [form="♀ (female)"]
  AD = female pin header, 6 pins [form="♀ (female)"]
  Power = female pin header, 8 pins [form="♀ (female)"]
  D_IF_3 = double row male pin header, 4 pins [form="♂ (male)"]
  D_IF_4 = double row male pin header, 4 pins [form="♂ (male)"]
  D_IF_2 = double row male pin header, 4 pins [form="♂ (male)"]
  AD_IF_1 = double row male pin header, 4 pins [form="♂ (male)"]
  AD_IF_4 = double row male pin header, 4 pins [form="♂ (male)"]
  AD_IF_3 = double row male pin header, 4 pins [form="♂ (male)"]
  D_IF_1 = double row male pin header, 4 pins [form="♂ (male)"]
  AD_switch1 = Akizuki slide switch IS-2235
  AD_switch2 = Akizuki slide switch IS-2235
  AD_switch4 = Akizuki slide switch IS-2235
  D_switch1 = Akizuki slide switch IS-2235
  D_switch2 = Akizuki slide switch IS-2235
  D_switch3 = Akizuki slide switch IS-2235
  D_switch4 = Akizuki slide switch IS-2235
  AD_IF_2 = double row male pin header, 4 pins [form="♂ (male)"]
  J1 = male pin header, 2 pins [form="♂ (male)"]
  AD_switch3 = Akizuki slide switch IS-2235
  AE-MOD1 = M-04522

nets:
  N1: IOL.pin2, D_switch2.pin1, D_switch2.pin5
  N2: IOL.pin5, D_switch1.pin1, D_switch1.pin5
  N3: IOH.pin6, D_switch4.pin1, D_switch4.pin5
  N4: IOH.pin7, D_switch3.pin1, D_switch3.pin5
  N5: AD.pin1, AD_switch1.pin1, AD_switch1.pin5
  N6: AD.pin2, AD_switch2.pin1, AD_switch2.pin5
  N7: AD.pin3, AD_switch3.pin1, AD_switch3.pin5
  N8: AD.pin4, AD_switch4.pin1, AD_switch4.pin5
  N9: Power.pin4, AE-MOD1.VCCA
  N10: Power.pin5, D_IF_3.pin3, D_IF_4.pin3, D_IF_2.pin3, AD_IF_1.pin2, AD_IF_4.pin2, AD_IF_3.pin2, D_IF_1.pin2, AD_IF_2.pin2, AE-MOD1.VCCB
  N11: Power.pin6, Power.pin7, D_IF_3.pin4, D_IF_4.pin4, D_IF_2.pin4, AD_IF_1.pin1, AD_IF_4.pin1, AD_IF_3.pin1, D_IF_1.pin1, AD_IF_2.pin1, J1.pin1, AE-MOD1.GND
  N12: D_IF_3.pin1, D_IF_2.pin2, D_switch3.pin4
  N13: D_IF_3.pin2, D_IF_4.pin1, D_switch4.pin4
  N14: D_IF_2.pin1, D_IF_1.pin3, D_switch2.pin4
  N15: AD_IF_1.pin3, AD_switch2.pin4, AD_IF_2.pin4
  N16: AD_IF_1.pin4, AD_switch1.pin4
  N17: AD_IF_4.pin3, D_IF_1.pin4, D_switch1.pin4
  N18: AD_IF_4.pin4, AD_IF_3.pin3, AD_switch4.pin4
  N19: AD_IF_3.pin4, AD_IF_2.pin3, AD_switch3.pin4
  N20: AD_switch1.pin0, AE-MOD1.A0
  N21: AD_switch1.pin3, AE-MOD1.B0
  N22: AD_switch2.pin0, AE-MOD1.A2
  N23: AD_switch2.pin3, AE-MOD1.B1
  N24: AD_switch4.pin0, AE-MOD1.A3
  N25: AD_switch4.pin3, AE-MOD1.B3
  N26: D_switch1.pin0, AE-MOD1.A4
  N27: D_switch1.pin3, AE-MOD1.B4
  N28: D_switch2.pin0, AE-MOD1.A5
  N29: D_switch2.pin3, AE-MOD1.B5
  N30: D_switch3.pin0, AE-MOD1.A6
  N31: D_switch3.pin3, AE-MOD1.B6
  N32: D_switch4.pin0, AE-MOD1.A7
  N33: D_switch4.pin3, AE-MOD1.B7
  N34: J1.pin2, AE-MOD1.OE
  N35: AD_switch3.pin0, AE-MOD1.A1
  N36: AD_switch3.pin3, AE-MOD1.B2

custom parts:
  Akizuki slide switch IS-2235: Akizuki slide switch is-2235 (P-02627)
  M-04522: Akizuki 8bit bi-directional logic level converter M-04522
