# Fritzing sketch マイクロSD両用シールド (saved by Fritzing 0.9.2b)
perfboards: 1

parts:
  IOL = female pin header, 8 pins [form="♀ (female)"]
  IOH = female pin header, 10 pins [form="♀ (female)"]
  AD = female pin header, 6 pins [form="♀ (female)"]  # not connected
  POWER = female pin header, 8 pins [form="♀ (female)"]
  J1 = Arduino R3 6pin male header [package=THT]  # not connected
  J2 = male pin header, 12 pins [form="♂ (male)"]
  Chip_select = male pin header, 12 pins [form="♂ (male)"]
  microSD1 = MicroSD Breakout
  J3 = male pin header, 12 pins [form="♂ (male)"]
  Card_detect = male pin header, 12 pins [form="♂ (male)"]
  S2 = Akizuki slide switch IS-2235

nets:
  N1: IOL.pin1, J2.pin5, J3.pin5
  N2: IOL.pin2, J2.pin6, J3.pin6
  N3: IOL.pin3, J2.pin7, J3.pin7
  N4: IOL.pin4, J2.pin8, J3.pin8
  N5: IOL.pin5, J2.pin9, J3.pin9
  N6: IOL.pin6, J2.pin10, J3.pin10
  N7: IOL.pin7, J2.pin11, J3.pin11
  N8: IOL.pin8, J2.pin12, J3.pin12
  GND: IOH.pin4, POWER.pin6, POWER.pin7, microSD1.GND
  SCLK: IOH.pin5, microSD1.CLK
  MISO: IOH.pin6, microSD1.DO
  MOSI: IOH.pin7, microSD1.DI
  N9: IOH.pin8, J2.pin1, J3.pin1
  N10: IOH.pin9, J2.pin2, J3.pin2
  N11: IOH.pin10, J2.pin3, J3.pin3
  N12: POWER.pin4, S2.pin5
  N13: POWER.pin5, S2.pin0
  Chip Select: Chip_select.pin1, Chip_select.pin2, Chip_select.pin3, Chip_select.pin4, Chip_select.pin5, Chip_select.pin6, Chip_select.pin7, Chip_select.pin8, Chip_select.pin9, Chip_select.pin10, Chip_select.pin11, Chip_select.pin12, microSD1.CS
  Card detect: microSD1.CD, Card_detect.pin1, Card_detect.pin2, Card_detect.pin3, Card_detect.pin4, Card_detect.pin5, Card_detect.pin6, Card_detect.pin7, Card_detect.pin8, Card_detect.pin9, Card_detect.pin10, Card_detect.pin11, Card_detect.pin12
  N14: microSD1.3v, S2.pin4
  N15: microSD1.5V, S2.pin1

custom parts:
  Arduino R3 6pin male header: Pin header for arduino R3
  MicroSD Breakout: 5V-ready microSD Breakout with Level Shifter
  Akizuki slide switch IS-2235: Akizuki slide switch is-2235 (P-02627)
