# Fritzing sketch Xbeeホスト基板(昇圧電源) (saved by Fritzing 0.9.2b)
perfboards: 1

parts:
  Reset = Momentary Switch [package=ksa_sealed_tac_switch]
  Xbee = XBEE-1 [package=xbee-1]
  IOL = female pin header, 8 pins [form="♀ (female)"]
  IOH = female pin header, 10 pins [form="♀ (female)"]
  AD = female pin header, 6 pins [form="♀ (female)"]
  Power = female pin header, 8 pins [form="♀ (female)"]
  J1 = male pin header, 3 pins [form="♂ (male)"]
  R1 = Resistor [tolerance=±5% resistance=10k package=THT]
  Vol = Trimmer Potentiometer [maximum_resistance=0.1MΩ package=THT]
  J2 = Arduino R3 6pin male header [package=THT]  # not connected
  Power_plug1 = Power plug
  AE-MOD1 = AE-XCL101C331BR-G
  Xbee1 = SSCI-KIT-XBSOCKET  # not connected

nets:
  N1: Reset.1, R1.Pin_0
  N2: Reset.2, Xbee.RESET, Power.pin3
  GND: Reset.3, Xbee.GND, IOH.pin4, Power.pin6, Power.pin7, J1.pin3, Vol.leg2, Power_plug1.GND, AE-MOD1.VSS
  3.3V: Xbee.VDD, Power.pin4, R1.Pin_1, Vol.leg1, AE-MOD1.Vout
  N3: Xbee.DOUT, IOL.pin7
  N4: Xbee.DIN, IOL.pin8
  N5: Xbee.DIO12, IOH.pin6
  N6: Xbee.RSSI, IOH.pin8
  N7: Xbee.DIO11, IOH.pin7
  N8: Xbee.RES, J1.pin2
  N9: Xbee.DTR, IOH.pin10
  N10: Xbee.DIO4, IOL.pin4
  N11: Xbee.CTS, IOL.pin1
  N12: Xbee.DIO9, IOL.pin5
  N13: Xbee.DIO5, IOL.pin3
  N14: Xbee.RTS, IOL.pin2
  N15: Xbee.DIO3, AD.pin4
  N16: Xbee.DIO2, AD.pin3
  N17: Xbee.DIO1, AD.pin2
  N18: Xbee.DIO0, AD.pin1
  VIN: Power.pin8, Power_plug1.VCC, AE-MOD1.Vbat, AE-MOD1.CE
  N19: J1.pin1, Vol.wiper

custom parts:
  Arduino R3 6pin male header: Pin header for arduino R3
  Power plug: 秋月電子通商 AE-DC-POWER-JACK-DIP(通販コードK-05148)とその互換品
  SSCI-KIT-XBSOCKET: Xbee pin conversion
